// Logisim project f.circ as structural Verilog: 1 circuit, main circuit main
module main (
);

  wire and_1_out, and_2_out, and_3_out, and_4_out, and_5_out, and_6_out, and_7_out, button_1_out,
       button_2_out, button_3_out, button_4_out, button_5_out, clock_1_out, s_r_ff_1_q, s_r_ff_1_qn,
       s_r_ff_2_q, s_r_ff_2_qn, s_r_ff_3_q, s_r_ff_3_qn, s_r_ff_4_q, s_r_ff_4_qn;

  Clock clock_1 (.out(clock_1_out));
  Button button_1 (.out(button_1_out));
  Button button_2 (.out(button_2_out));
  Button button_3 (.out(button_3_out));
  Button button_4 (.out(button_4_out));
  Button button_5 (.out(button_5_out));
  and and_1 (and_1_out, button_1_out, and_5_out);
  and and_2 (and_2_out, button_2_out, and_5_out);
  and and_3 (and_3_out, button_3_out, and_5_out);
  and and_4 (and_4_out, button_4_out, and_5_out);
  S_R_Flip_Flop s_r_ff_1 (
    .S(and_1_out), .clk(clock_1_out), .R(button_5_out), .Q(s_r_ff_1_q), .Qn(s_r_ff_1_qn));  // open: preset, reset, en
  S_R_Flip_Flop s_r_ff_2 (
    .S(and_2_out), .clk(clock_1_out), .R(button_5_out), .Q(s_r_ff_2_q), .Qn(s_r_ff_2_qn));  // open: preset, reset, en
  S_R_Flip_Flop s_r_ff_3 (
    .S(and_3_out), .clk(clock_1_out), .R(button_5_out), .Q(s_r_ff_3_q), .Qn(s_r_ff_3_qn));  // open: preset, reset, en
  S_R_Flip_Flop s_r_ff_4 (
    .S(and_4_out), .clk(clock_1_out), .R(button_5_out), .Q(s_r_ff_4_q), .Qn(s_r_ff_4_qn));  // open: preset, reset, en
  and and_5 (and_5_out, and_6_out, and_7_out);
  and and_6 (and_6_out, s_r_ff_1_qn, s_r_ff_2_qn);
  and and_7 (and_7_out, s_r_ff_3_qn, s_r_ff_4_qn);
  LED led_1 (.in(s_r_ff_3_q));
  LED led_2 (.in(s_r_ff_4_q));
  LED led_3 (.in(s_r_ff_1_q));
  LED led_4 (.in(s_r_ff_2_q));
endmodule
