// Logisim project final.circ as structural Verilog: 1 circuit, main circuit main
module main (
  output BUZZER
);

  wire and_1_out, and_2_out, and_3_out, and_4_out, and_5_out, and_6_out, and_7_out, button_1_out,
       button_2_out, button_3_out, button_4_out, button_5_out, s_r_ff_1_q, s_r_ff_1_qn, s_r_ff_2_q,
       s_r_ff_2_qn, s_r_ff_3_q, s_r_ff_3_qn, s_r_ff_4_q, s_r_ff_4_qn;

  Button button_1 (.out(button_1_out));
  Button button_2 (.out(button_2_out));
  Button button_3 (.out(button_3_out));
  Button button_4 (.out(button_4_out));
  Button button_5 (.out(button_5_out));
  and and_1 (and_1_out, button_1_out, and_5_out);
  and and_2 (and_2_out, button_2_out, and_5_out);
  and and_3 (and_3_out, button_3_out, and_5_out);
  and and_4 (and_4_out, button_4_out, and_5_out);
  S_R_Flip_Flop s_r_ff_1 (
    .Q(s_r_ff_1_q), .Qn(s_r_ff_1_qn), .preset(and_1_out), .reset(button_5_out));  // open: S, clk, R, en
  S_R_Flip_Flop s_r_ff_2 (
    .Q(s_r_ff_2_q), .Qn(s_r_ff_2_qn), .preset(and_2_out), .reset(button_5_out));  // open: S, clk, R, en
  S_R_Flip_Flop s_r_ff_3 (
    .Q(s_r_ff_3_q), .Qn(s_r_ff_3_qn), .preset(and_3_out), .reset(button_5_out));  // open: S, clk, R, en
  S_R_Flip_Flop s_r_ff_4 (
    .Q(s_r_ff_4_q), .Qn(s_r_ff_4_qn), .preset(and_4_out), .reset(button_5_out));  // open: S, clk, R, en
  and and_5 (and_5_out, and_6_out, and_7_out);
  and and_6 (and_6_out, s_r_ff_1_qn, s_r_ff_2_qn);
  and and_7 (and_7_out, s_r_ff_3_qn, s_r_ff_4_qn);
  LED led_1 (.in(s_r_ff_1_q));
  LED led_2 (.in(s_r_ff_2_q));
  LED led_3 (.in(s_r_ff_3_q));
  LED led_4 (.in(s_r_ff_4_q));
  or or_1 (BUZZER, s_r_ff_1_q, s_r_ff_2_q, s_r_ff_3_q, s_r_ff_4_q);

  // Notes on the sheet:
  //   PLAYER 1
  //   PLAYER 2
  //   PLAYER 3
  //   PLAYER 4
  //   RESET
  //   FASTEST FINGER FIRST
  //   PLAYER 3 INDICATOR
  //   PLAYER 1 INDICATOR
  //   PLAYER 2 INDICATOR
  //   PLAYER 4 INDICATOR
endmodule
